# Fritzing sketch circuit (saved by Fritzing 0.9.3b)

parts:
  부품3 = Adafruit AMG8833 8x8 GRID EYE
  부품4 = Arduino Uno (Rev3)

nets:
  VIN: 부품3.VIN, 부품4.5V
  GND: 부품3.GND, 부품4.GND
  N1: 부품3.RXD, 부품4.D2
  N2: 부품3.TXD, 부품4.D3_PWM
